# Fritzing sketch accelerometer (saved by Fritzing 0.9.2b)
breadboards: 1

parts:
  Part1 = Arduino Uno (Rev3)
  3-Axis_Accelerometer1 = 3-Axis Accelerometer Breakout - MMA8452Q
  R6 = Resistor [tolerance=±5% resistance=220 package=THT]
  R7 = Resistor [tolerance=±5% resistance=220 package=THT]

nets:
  N1: Part1.A4/SDA, R7.Pin_0
  N2: Part1.A5/SCL, R6.Pin_0
  3V3: Part1.3V3, 3-Axis_Accelerometer1.3.3V
  GND: Part1.GND, 3-Axis_Accelerometer1.GND
  N3: 3-Axis_Accelerometer1.SDA, R7.Pin_1
  N4: 3-Axis_Accelerometer1.SCL, R6.Pin_1

notes:
  330 Ω
