# Fritzing sketch flex (saved by Fritzing 0.9.2b)
breadboards: 1

parts:
  Part1 = Arduino Uno (Rev3)
  R2 = Basic Flex Resistor
  R5 = Resistor [tolerance=±5% resistance=22k package="0402 [SMD]"]

nets:
  N1: Part1.A0, R2.pin_1, R5.Pin_1
  N2: Part1.5V, R2.Pin_2
  N3: Part1.GND, R5.Pin_0

notes:
  22 kΩ
