# Fritzing sketch force (saved by Fritzing 0.9.2b)
breadboards: 1

parts:
  Part1 = Arduino Uno (Rev3)
  R5 = Resistor [tolerance=±5% resistance=10k package="0402 [SMD]"]
  J1 = Basic Force Sensing Resistor (FSR) [package=THT]

nets:
  N1: Part1.A3, R5.Pin_1, J1.pin_1
  N2: Part1.5V, J1.pin_0
  N3: Part1.GND, R5.Pin_0

notes:
  10 kΩ
