# Fritzing sketch hall-effect (saved by Fritzing 0.9.2b)
breadboards: 1

parts:
  Part1 = Arduino Uno (Rev3)
  R5 = Resistor [tolerance=±5% resistance=10k package="0402 [SMD]"]
  U2 = mystery part, 3 pins [chip_label=1881]

nets:
  N1: Part1.A3, R5.Pin_0, U2.pin3
  N2: Part1.5V, R5.Pin_1, U2.pin1
  N3: Part1.GND, U2.pin2

notes:
  10 kΩ
