# Fritzing sketch piezo (saved by Fritzing 0.9.2b)
breadboards: 1

parts:
  Part1 = Arduino Uno (Rev3)
  R5 = Resistor [tolerance=±5% resistance=1M package="0402 [SMD]"]
  J2 = Piezo Speaker

nets:
  N1: Part1.A4/SDA, R5.Pin_1, J2.pin2
  N2: Part1.GND, R5.Pin_0, J2.pin1

notes:
  1 MΩ
