# Fritzing sketch pot (saved by Fritzing 0.9.2b)
breadboards: 1

parts:
  Part1 = Arduino Uno (Rev3)
  R4 = TRIMPOT [package=3362u-2]

nets:
  N1: Part1.A4/SDA, R4.WIPER
  N2: Part1.5V, R4.CW
  N3: Part1.GND, R4.CCW
