# Fritzing sketch reed-switch (saved by Fritzing 0.9.2b)
breadboards: 1

parts:
  Part1 = Arduino Uno (Rev3)
  R5 = Resistor [tolerance=±5% resistance=10k package="0402 [SMD]"]
  S1 = SWITCH-MOMENTARY-2 [package=reed_switch_plastic]

nets:
  N1: Part1.D6_PWM, R5.Pin_0, S1.1
  N2: Part1.5V, S1.2
  N3: Part1.GND, R5.Pin_1

notes:
  10 kΩ
