# Fritzing sketch temperature (saved by Fritzing 0.9.2b)
breadboards: 1

parts:
  Part1 = Arduino Uno (Rev3)
  T1 = TMP36 Temperature Sensor [package="TO92 [THT]"]

nets:
  N1: Part1.A5/SCL, T1.Vout
  N2: Part1.5V, T1.+Vs
  GND: Part1.GND, T1.GND
