# Fritzing sketch tilt (saved by Fritzing 0.9.2b)
breadboards: 1

parts:
  Part1 = Arduino Uno (Rev3)
  R5 = Resistor [tolerance=±5% resistance=1k package="0402 [SMD]"]
  S2 = Tilt Switch [package=THT]

nets:
  N1: Part1.D7, R5.Pin_0, S2.Pin_1
  N2: Part1.5V, R5.Pin_1
  N3: Part1.GND, S2.Pin_2

notes:
  1 kΩ
